# Fritzing sketch nhd (saved by Fritzing 0.6.5b)
breadboards: 1

parts:
  U1 = SIP - 20 pins [package="SIP (Single Inline) [THT]"]
  IC1 = IC, DIP package, 16 pins [chip_label=74HC4050 spacing=300mil]
  Arduino1 = Arduino
  R1 = Resistor [tolerance=±5% resistance=10k package=THT]
  C1 = Ceramic Capacitor [capacitance=1µF package="100 mil [THT, multilayer]"]

nets:
  N1: U1.D/C, IC1.pin12
  N2: U1.R/W, U1.E, U1.DB3, U1.DB4, U1.DB5, U1.DB6, U1.DB7, U1.BS2, U1.BS1, IC1.pin3, IC1.pin5, IC1.pin8, Arduino1.GND, C1.0
  N3: U1.DB0, IC1.pin15
  N4: U1.DB1, IC1.pin6
  N5: U1./RES, R1.Pin_1, C1.1
  N6: U1./CS, IC1.pin10
  N7: IC1.pin1, Arduino1.3V3, R1.Pin_0
  N8: IC1.pin7, Arduino1.D11
  N9: IC1.pin9, Arduino1.D10
  N10: IC1.pin11, Arduino1.D9
  N11: IC1.pin14, Arduino1.D13

custom parts:
  SIP - 20 pins: A SIP stand-in part for whatever you want. With 20 pins on a 300 mil single inline package (SIP) footprint.
